// Digital circuit alu.dig as structural Verilog
module alu (
  input  [15:0] ADD_instr,
  input  [15:0] D_cache,
  output [1:0] rs_1,
  output [15:0] D_res,
  output [1:0] rd,
  output en,
  output ovf
);

  Add #(.Bits(16)) add_1 (.a(D_cache), .b({{6{1'b0}}, ADD_instr[15:6]}), .c_i(1'b0), .s(D_res), .c_o(ovf));

  assign en = ADD_instr[2];
  assign rd = ADD_instr[5:4];
  assign rs_1 = ADD_instr[5:4];
endmodule
