// Digital circuit cache.dig as structural Verilog
module cache (
  input  [15:0] LD_instr,
  input  [15:0] RAM_i,
  input  C,
  input  [15:0] ST_instr,
  output [5:0] addr,
  output ld,
  output [15:0] D_o,
  output st,
  output [15:0] RAM_o
);

  wire decoder_1_out_0;
  wire [1:0] priorityencoder_1_num, rs;
  wire [4:0] demultiplexer_2_out_0;
  wire [4:2] demultiplexer_2_out_1;
  wire [5:0] ld_addr;
  wire [8:0] demultiplexer_1_out_0;
  wire [8:6] demultiplexer_1_out_1;
  wire [15:0] multiplexer_1_out;

  // Probe on LD_instr[3:1]
  Decoder decoder_1 (.sel(LD_instr[6]), .out_0(decoder_1_out_0), .out_1(ld));
  // Probe on decoder_1_out_0
  Demultiplexer #(.Bits(9)) demultiplexer_1 (
    .sel(LD_instr[6]), .in(LD_instr[15:7]), .out_0(demultiplexer_1_out_0),
    .out_1({demultiplexer_1_out_1, ld_addr}));
  Demultiplexer #(.Bits(5)) demultiplexer_2 (
    .sel(ST_instr[10]), .in(ST_instr[15:11]), .out_0(demultiplexer_2_out_0),
    .out_1({demultiplexer_2_out_1, rs}));
  PriorityEncoder #(.Selector_Bits(2)) priorityencoder_1 (
    .in0(1'b1), .in1(ld), .in2(ST_instr[1]), .in3(1'b0), .num(priorityencoder_1_num));  // open: any
  Multiplexer #(.Bits(16)) multiplexer_1 (
    .sel(LD_instr[6]), .in_0({{7{1'b0}}, demultiplexer_1_out_0}), .in_1(RAM_i), .out(multiplexer_1_out));
  Multiplexer #(.Bits(16)) multiplexer_2 (
    .sel(ST_instr[10]), .in_0({{11{1'b0}}, demultiplexer_2_out_0}), .in_1(D_o), .out(RAM_o));
  regfile regfile_1 (.en(LD_instr[0]), .rd(LD_instr[5:4]), .D_i(multiplexer_1_out), .C(C), .rs(rs), .D_o(D_o));
  Multiplexer #(.Selector_Bits(2), .Bits(6)) multiplexer_3 (
    .sel(priorityencoder_1_num), .in_0({6{1'b0}}), .in_1(ld_addr), .in_2(ST_instr[9:4]), .in_3({6{1'b0}}),
    .out(addr));

  assign st = ST_instr[1];

  // Other names for the same wires on the sheet: st_addr[5:0] = ST_instr[9:4]
endmodule
