// Digital circuit fetch.dig as structural Verilog
module fetch (
  input  C,
  output error,
  output halt,
  output [15:0] D_o,
  output [15:0] D_o2
);

  wire alu_1_en, C_t, decoder_1_out_0, decoder_2_p3, err, ld_en, st_en;
  wire [1:0] alu_1_rd, alu_1_rs_1, alu_1_rs_2, priorityencoder_1_num;
  wire [5:0] _1A, PC_out;
  wire [15:0] add, addr, alu_1_d_res, D_in, halt_t, IR_q, load, ramdualaccess_1_d1, ramdualaccess_1_d2, store;

  PriorityEncoder #(.Selector_Bits(2)) priorityencoder_1 (
    .in0(1'b1), .in1(halt_t[0]), .in2(err), .in3(1'b0), .num(priorityencoder_1_num));  // open: any
  Counter #(.Bits(6)) PC (.en(1'b1), .C(C_t), .clr(1'b0), .out(PC_out), .ovf(err));
  Decoder #(.Selector_Bits(2)) decoder_1 (
    .sel(priorityencoder_1_num), .out_0(decoder_1_out_0), .out_1(halt), .out_2(error));  // open: out_3
  alu alu_1 (
    .D_1(D_o), .D_2(D_o2), .ADD_instr(add), .ADDR_instr(addr), .rs_1(alu_1_rs_1), .D_res(alu_1_d_res),
    .rd(alu_1_rd), .en(alu_1_en), .rs_2(alu_1_rs_2));  // open: ovf
  and and_1 (C_t, C, decoder_1_out_0);
  RAMDualAccess #(.AddrBits(6), .isProgramMemory("true"), .Bits(16)) ramdualaccess_1 (
    .str(st_en), .C(C_t), .ld(ld_en), .A1(_1A), .Din1(D_in), .A2(PC_out), .D1(ramdualaccess_1_d1),
    .D2(ramdualaccess_1_d2));
  cache cache_1 (
    .LD_instr(load), .RAM_i(ramdualaccess_1_d1), .C(C_t), .ST_instr(store), .rs_1(alu_1_rs_1),
    .D_in(alu_1_d_res), .rd(alu_1_rd), .en(alu_1_en), .rs_2(alu_1_rs_2), .addr(_1A), .ld(ld_en), .st(st_en),
    .RAM_o(D_in), .D_o1(D_o), .D_o2(D_o2));  // open: rs_3, D_o3
  Register #(.Bits(16)) IR (.D(ramdualaccess_1_d2), .C(C_t), .en(1'b1), .Q(IR_q));
  // decoder decoder_2: pin names not known; wires that end beside it: IR_q, C_t, decoder_2_p3, load, store, add, addr, halt_t
  // Probe on decoder_2_p3
endmodule
